# Fritzing sketch Bumpometer for optimized PCB2 (saved by Fritzing 0.9.2b)
circuit board: 29.1376cm x 19.6031cm
breadboards: 1

parts:
  Part5 = Arduino Uno (Rev3)
  Part6 = Arduino Mega 2560 (Rev3)
  JP2 = Header 12 [package=1x12_machine-pin-header_lock.004]
  U7 = LIPO-2000mAh [package=lipo-2000]
  GY3 = MPU-6050 Board GY-521 [form="♀ (female)" package=THT]
  U8 = LCD-16X2 [package=lcd-16x2_noholes]
  R7 = Resistor [tolerance=±5% resistance=220 package="0402 [SMD]"]
  R8 = TRIMPOT [package=3362u-2]
  U9 = SUP500F [package=sup500f]

nets (from the breadboard view):
  N1: Part5.A4/SDA, Part6.D20/SDA, Part6.SDA, GY3.pin4
  N2: Part5.A5/SCL, Part6.D21/SCL, Part6.SCL, GY3.pin3
  N3: Part5.D10_PWM/SS, U9.TX
  N4: Part5.D11_PWM/MOSI, U9.RX
  GND: Part5.GND, Part6.GND, JP2.1, U7.-, GY3.pin2, U8.VSS, U8.R_W, U8.K, R8.CCW, U9.GND
  3V3: Part5.3V3, U9.VCC
  VIN: Part5.VIN, Part6.VIN, U7.+
  N5: Part6.D12_PWM, U8.RS
  N6: Part6.D11_PWM, U8.E
  N7: Part6.RESET, Part6.D7_PWM
  5V: Part6.5V, JP2.2, GY3.pin1, U8.VDD, R7.Pin_0, R8.CW
  N8: Part6.D3_PWM, U8.DB7
  N9: Part6.D4_PWM, U8.DB6
  N10: Part6.D5_PWM, U8.DB5
  N11: Part6.D6_PWM, U8.DB4
  N12: Part6.D50, JP2.3
  N13: Part6.D51, JP2.4
  N14: Part6.D52, JP2.5
  N15: Part6.D53, JP2.6
  N16: U8.VO, R8.WIPER
  N17: U8.A, R7.Pin_1

custom parts:
  MPU-6050 Board GY-521: Acelerometro y Giroscopio MPU-6050 Board GY-521
  SUP500F: SUP500F Venus GPS
