# Fritzing sketch Bumpometer wo int2 (saved by Fritzing 0.9.2b)
circuit board: 8.46667cm x 5.64444cm
breadboards: 1

parts:
  Part1 = Arduino Uno (Rev3)
  Part2 = Arduino Mega 2560 (Rev3)
  U1 = SUP500F [package=sup500f]
  GY1 = MPU-6050 Board GY-521 [form="♀ (female)" package=THT]
  R1 = Resistor [tolerance=±5% resistance=220 package="0402 [SMD]"]
  U2 = LCD-16X2 [package=lcd-16x2_noholes]
  R2 = TRIMPOT [package=3362u-2]
  R3 = Resistor [tolerance=±5% resistance=220 package="2512 [SMD]"]
  SD_card_module1 = SD Card Module
  U3 = LIPO-2000mAh [package=lipo-2000]

nets (from the breadboard view):
  N1: Part1.A4/SDA, Part2.D20/SDA, GY1.pin4
  N2: Part1.A5/SCL, Part2.D21/SCL, Part2.SCL, GY1.pin3
  N3: Part1.D10_PWM/SS, U1.TX
  N4: Part1.D11_PWM/MOSI, U1.RX
  GND: Part1.GND, Part2.GND, U1.GND, GY1.pin2, U2.VSS, U2.R_W, U2.K, R2.CCW, R3.Pin_0, SD_card_module1.GND, U3.-
  3V3: Part1.3V3, U1.VCC
  VIN: Part1.VIN, Part2.VIN, U3.+
  N5: Part2.D12_PWM, U2.RS
  N6: Part2.D11_PWM, U2.E
  N7: Part2.RESET, Part2.D7_PWM, R3.Pin_1
  5V: Part2.5V, GY1.pin1, R1.Pin_0, U2.VDD, R2.CW, SD_card_module1.+5
  N8: Part2.D3_PWM, U2.DB7
  N9: Part2.D4_PWM, U2.DB6
  N10: Part2.D5_PWM, U2.DB5
  N11: Part2.D6_PWM, U2.DB4
  N12: Part2.D50, SD_card_module1.MISO
  N13: Part2.D51, SD_card_module1.MOSI
  N14: Part2.D52, SD_card_module1.SCK
  N15: Part2.D53, SD_card_module1.CS
  N16: R1.Pin_1, U2.A
  N17: U2.VO, R2.WIPER

custom parts:
  SUP500F: SUP500F Venus GPS
  MPU-6050 Board GY-521: Acelerometro y Giroscopio MPU-6050 Board GY-521
  SD Card Module: SD Card Module Slot Socket Reader For Arduino ARM MCU
