# Fritzing sketch Environmental Analyst (saved by Fritzing 0.9.2b)

parts:
  Part1 = Arduino Cellular Shield
  JP5 = Header 2 [package=springterminal-2.54mm-2]
  JP6 = Header 2 [package=springterminal-2.54mm-2]
  RHT2 = Humidity and Temperature Sensor RHT03

nets:
  N1: Part1.A0, JP6.1
  N2: Part1.D-RX, RHT2.Data-signal
  N3: Part1.D-TX, JP5.2
  N4: Part1.D4, JP5.1
  N5: Part1.D6, JP6.2

notes:
  Attach Pin#4 to Pin#4 of Dust Sensor
  Attach Pin#3 to Pin#2 of Dust Sensor
  Attach VCC & GND respectively
  Attach A0 to Aout of MQ7
  Attach Pin#6 to Dout of MQ7
  Attach VCC & GND respectively

custom parts:
  Humidity and Temperature Sensor RHT03: Digital relative humidity & temperature sensor RHT03
